# Fritzing sketch Obstruction Sensor PCB Sketch (saved by Fritzing 0.9.3b)
circuit board: 5.40156cm x 4.85174cm
breadboards: 1

parts:
  VL53L0X = Header 6 [package=molex-1x6_lock]
  SSD1306 = Header 4 [package=molex-1x4_lock]
  Raspberry_Pi1 = Raspberry Pi 2
  J1 = Dagu DGServo 9g header (male) [package=THT]

nets:
  N1: VL53L0X.1, SSD1306.2, Raspberry_Pi1.3v3
  N2: VL53L0X.2, SSD1306.1, Raspberry_Pi1.GND
  N3: VL53L0X.3, SSD1306.3, Raspberry_Pi1.GPIO3
  N4: VL53L0X.4, SSD1306.4, Raspberry_Pi1.GPIO2
  N5: VL53L0X.5, J1.Vcc
  N6: VL53L0X.6, J1.pulse

notes:
  VCC
  GND
  SCL
  SDA
  GPI01
  XSHUT
